// Logisim project bonus+studio.circ as structural Verilog: 1 circuit, main circuit main
module main (
  input  in_1
);

  wire CLK, multiplexer_1_out, Q0, Q1, Q2;
  wire [1:0] priority_encoder_1_out;
  wire [3:0] bit_extender_1_out;

  Clock clock_1 (.out(CLK));
  Priority_Encoder #(.select(2)) priority_encoder_1 (
    .in0(Q0), .in1(Q1), .in2(Q2), .in3(in_1), .out(priority_encoder_1_out), .en_in(1'b1));  // open: gs, en_out
  Hex_Digit_Display hex_digit_display_1 (.value(bit_extender_1_out));  // open: dp
  Multiplexer #(.select(3), .disabled(0), .enable("false")) multiplexer_1 (
    .in0(in_1), .in1(Q0), .in2(Q1), .in3(Q2), .in4(priority_encoder_1_out[1]),
    .in5(priority_encoder_1_out[0]), .in6(priority_encoder_1_out[1]), .in7(priority_encoder_1_out[0]),
    .out(multiplexer_1_out), .sel({Q2, Q1, Q0}));
  D_Flip_Flop d_ff_1 (.clk(CLK), .D(multiplexer_1_out), .Q(Q2));  // open: Qn, preset, en, reset
  assign bit_extender_1_out = {{1{1'b0}}, {Q2, Q1, Q0}};  // Bit_Extender bit_extender_1
  D_Flip_Flop d_ff_2 (.clk(CLK), .D(Q2), .Q(Q1));  // open: Qn, preset, en, reset
  D_Flip_Flop d_ff_3 (.clk(CLK), .D(Q1), .Q(Q0));  // open: Qn, preset, en, reset

  // Other names for the same wires on the sheet: Input_X = in_1
endmodule
