// Logisim project Studio+1+Skeleton.circ as structural Verilog: 1 circuit, main circuit studio 1
module studio_1 (
  input  [3:0] in_1,
  output open_the_second_register,
  output close_the_second_register
);

  wire nand_1_out, not_1_out, or_1_out;

  Hex_Digit_Display hex_digit_display_1 (.value(in_1));  // open: dp
  or or_1 (or_1_out, in_1[2], in_1[1]);
  nand nand_1 (nand_1_out, in_1[2], in_1[1]);
  not not_1 (not_1_out, in_1[3]);
  and and_1 (close_the_second_register, not_1_out, nand_1_out);
  and and_2 (open_the_second_register, in_1[3], or_1_out);

  // Other names for the same wires on the sheet: n0 = in_1[0]; n1 = in_1[1]; n2 = in_1[2]; n3 = in_1[3]

  // Notes on the sheet:
  //   These are your inputs, you can connect wires from these "tunnels" above to the inputs of your gates
  //   You can use the poke tool in this 4 bit box to indicate the number of people waiting in line.    It will be displayed on the display.
  //   These are your outputs and should be connected to the outputs of your gates
endmodule
