// Logisim project studio10.circ as structural Verilog: 7 circuits, main circuit 16bit ripplecarry
module _16bit_ripplecarry (
  input  carry_in,
  input  in_2,
  input  in_3,
  input  in_4,
  input  in_5,
  input  in_6,
  input  in_7,
  input  in_8,
  input  in_9,
  input  in_10,
  input  in_11,
  input  in_12,
  input  in_13,
  input  in_14,
  input  in_15,
  input  in_16,
  input  in_17,
  input  in_18,
  input  in_19,
  input  in_20,
  input  in_21,
  input  in_22,
  input  in_23,
  input  in_24,
  input  in_25,
  input  in_26,
  input  in_27,
  input  in_28,
  input  in_29,
  input  in_30,
  input  in_31,
  input  Addend_B,
  input  Addend_A,
  output s0,
  output s1,
  output s2,
  output s3,
  output s4,
  output s5,
  output s6,
  output s7,
  output s8,
  output s9,
  output s10,
  output s11,
  output s12,
  output s13,
  output s14,
  output s15,
  output Overflow
);

  wire adder_1_cout, adder_2_cout, adder_3_cout, adder_4_cout, adder_5_cout, adder_6_cout, adder_7_cout,
       adder_8_cout, adder_9_cout, adder_10_cout, adder_11_cout, adder_12_cout, adder_13_cout, adder_14_cout,
       adder_15_cout, xnor_1_out, xor_1_out;

  xnor xnor_1 (xnor_1_out, Addend_A, Addend_B);
  and and_1 (Overflow, xnor_1_out, xor_1_out);
  Adder #(.width(1)) adder_1 (.a(in_2), .b(in_3), .out(s0), .cin(carry_in), .cout(adder_1_cout));
  Adder #(.width(1)) adder_2 (.a(in_4), .b(in_5), .out(s1), .cin(adder_1_cout), .cout(adder_2_cout));
  Adder #(.width(1)) adder_3 (.a(in_6), .b(in_7), .out(s2), .cin(adder_2_cout), .cout(adder_3_cout));
  Adder #(.width(1)) adder_4 (.a(in_8), .b(in_9), .out(s3), .cin(adder_3_cout), .cout(adder_4_cout));
  Adder #(.width(1)) adder_5 (.a(in_10), .b(in_11), .out(s4), .cin(adder_4_cout), .cout(adder_5_cout));
  Adder #(.width(1)) adder_6 (.a(in_12), .b(in_13), .out(s5), .cin(adder_5_cout), .cout(adder_6_cout));
  Adder #(.width(1)) adder_7 (.a(in_14), .b(in_15), .out(s6), .cin(adder_6_cout), .cout(adder_7_cout));
  Adder #(.width(1)) adder_8 (.a(in_16), .b(in_17), .out(s7), .cin(adder_7_cout), .cout(adder_8_cout));
  Adder #(.width(1)) adder_9 (.a(in_18), .b(in_19), .out(s8), .cin(adder_8_cout), .cout(adder_9_cout));
  Adder #(.width(1)) adder_10 (.a(in_20), .b(in_21), .out(s9), .cin(adder_9_cout), .cout(adder_10_cout));
  Adder #(.width(1)) adder_11 (.a(in_22), .b(in_23), .out(s10), .cin(adder_10_cout), .cout(adder_11_cout));
  Adder #(.width(1)) adder_12 (.a(in_24), .b(in_25), .out(s11), .cin(adder_11_cout), .cout(adder_12_cout));
  Adder #(.width(1)) adder_13 (.a(in_26), .b(in_27), .out(s12), .cin(adder_12_cout), .cout(adder_13_cout));
  Adder #(.width(1)) adder_14 (.a(in_28), .b(in_29), .out(s13), .cin(adder_13_cout), .cout(adder_14_cout));
  Adder #(.width(1)) adder_15 (.a(in_30), .b(in_31), .out(s14), .cin(adder_14_cout), .cout(adder_15_cout));
  Adder #(.width(1)) adder_16 (.a(Addend_B), .b(Addend_A), .out(s15), .cin(adder_15_cout));  // open: cout
  xor xor_1 (xor_1_out, Addend_B, s15);
endmodule

module carry_lookahead (
  input  a3,
  input  b3,
  input  a2,
  input  b2,
  input  a1,
  input  b1,
  input  a0,
  input  b0,
  input  Carry_in,
  output s3,
  output s2,
  output s1,
  output s0,
  output Carry_out
);

  wire and_2_out, and_3_out, and_4_out, and_6_out, and_7_out, and_8_out, and_10_out, and_11_out, and_13_out,
       and_14_out, C1, C2, C3, G0, G1, G2, G3, P0, P1, P2, P3;

  and and_1 (G3, a3, b3);
  and and_2 (and_2_out, P3, G2);
  and and_3 (and_3_out, P3, P2, G1);
  or or_1 (Carry_out, G3, and_2_out, and_3_out, and_4_out, and_6_out);
  xor xor_1 (P3, a3, b3);
  and and_4 (and_4_out, P3, P2, P1, G0);
  and and_5 (G2, a2, b2);
  xor xor_2 (s3, P3, C3);
  and and_6 (and_6_out, P3, P2, P1, P0, Carry_in);
  xor xor_3 (P2, a2, b2);
  and and_7 (and_7_out, P2, G1);
  and and_8 (and_8_out, P2, P1, G0);
  or or_2 (C3, G2, and_7_out, and_8_out, and_10_out);
  and and_9 (G1, a1, b1);
  xor xor_4 (s2, P2, C2);
  and and_10 (and_10_out, P2, P1, P0, Carry_in);
  xor xor_5 (P1, a1, b1);
  xor xor_6 (s1, P1, C1);
  and and_11 (and_11_out, P1, G0);
  or or_3 (C2, G1, and_11_out, and_13_out);
  and and_12 (G0, a0, b0);
  and and_13 (and_13_out, P1, P0, Carry_in);
  xor xor_7 (P0, a0, b0);
  xor xor_8 (s0, P0, Carry_in);
  or or_4 (C1, G0, and_14_out);
  and and_14 (and_14_out, P0, Carry_in);
endmodule

module _16bit_adder_with_overflow (
  input  a15,
  input  a14,
  input  a13,
  input  a12,
  input  a11,
  input  a10,
  input  a9,
  input  a8,
  input  a7,
  input  a6,
  input  a5,
  input  a4,
  input  a3,
  input  a2,
  input  a1,
  input  a0,
  input  b15,
  input  b14,
  input  b13,
  input  b12,
  input  b11,
  input  b10,
  input  b9,
  input  b8,
  input  b7,
  input  b6,
  input  b5,
  input  b4,
  input  b3,
  input  b2,
  input  b1,
  input  b0,
  input  carry_in,
  output s15,
  output s14,
  output s13,
  output s12,
  output s11,
  output s10,
  output s9,
  output s8,
  output s7,
  output s6,
  output s5,
  output s4,
  output s3,
  output s2,
  output s1,
  output s0,
  output Overflow
);

  wire carry_lookahead_1_s3, carry_lookahead_2_carry_out, carry_lookahead_3_carry_out,
       carry_lookahead_4_carry_out, xnor_1_out, xor_1_out;

  xnor xnor_1 (xnor_1_out, a15, b15);
  and and_1 (Overflow, xnor_1_out, xor_1_out);
  xor xor_1 (xor_1_out, b15, carry_lookahead_1_s3);
  carry_lookahead carry_lookahead_1 (
    .a3(a15), .b3(b15), .a2(a14), .b2(b14), .a1(a13), .b1(b13), .a0(a12), .b0(b12),
    .Carry_in(carry_lookahead_2_carry_out), .Carry_out(s15), .s3(carry_lookahead_1_s3), .s2(s14), .s1(s13),
    .s0(s12));
  carry_lookahead carry_lookahead_2 (
    .a3(a11), .b3(b11), .a2(a10), .b2(b10), .a1(a9), .b1(b9), .a0(a8), .b0(b8),
    .Carry_in(carry_lookahead_3_carry_out), .Carry_out(carry_lookahead_2_carry_out), .s3(s11), .s2(s10),
    .s1(s9), .s0(s8));
  carry_lookahead carry_lookahead_3 (
    .a3(a7), .b3(b7), .a2(a6), .b2(b6), .a1(a5), .b1(b5), .a0(a4), .b0(b4),
    .Carry_in(carry_lookahead_4_carry_out), .Carry_out(carry_lookahead_3_carry_out), .s3(s7), .s2(s6),
    .s1(s5), .s0(s4));
  carry_lookahead carry_lookahead_4 (
    .a3(a3), .b3(b3), .a2(a2), .b2(b2), .a1(a1), .b1(b1), .a0(a0), .b0(b0), .Carry_in(carry_in),
    .Carry_out(carry_lookahead_4_carry_out), .s3(s3), .s2(s2), .s1(s1), .s0(s0));
endmodule

module carry_lookahead_extension (
  input  a3,
  input  b3,
  input  a2,
  input  b2,
  input  a1,
  input  b1,
  input  a0,
  input  b0,
  input  Carry_in,
  output s3,
  output s2,
  output s1,
  output s0,
  output Carry_out,
  output G,
  output P
);

  wire and_6_out, and_8_out, and_9_out, and_11_out, and_12_out, and_14_out, and_15_out, C1, C2, C3, G0, g0_t,
       G1, g1_t, G2, g2_t, G3, P0, P1, P2, P3;

  and and_1 (G3, a3, b3);
  and and_2 (g1_t, P3, P2, G1);
  and and_3 (g2_t, P3, G2);
  or or_1 (Carry_out, G3, g2_t, g1_t, g0_t, and_6_out);
  xor xor_1 (P3, a3, b3);
  and and_4 (g0_t, P3, P2, P1, G0);
  and and_5 (G2, a2, b2);
  xor xor_2 (s3, P3, C3);
  and and_6 (and_6_out, P3, P2, P1, P0, Carry_in);
  and and_7 (P, P0, P1, P2, P3);
  xor xor_3 (P2, a2, b2);
  and and_8 (and_8_out, P2, G1);
  and and_9 (and_9_out, P2, P1, G0);
  or or_2 (C3, G2, and_8_out, and_9_out, and_11_out);
  and and_10 (G1, a1, b1);
  xor xor_4 (s2, P2, C2);
  and and_11 (and_11_out, P2, P1, P0, Carry_in);
  xor xor_5 (P1, a1, b1);
  xor xor_6 (s1, P1, C1);
  and and_12 (and_12_out, P1, G0);
  or or_3 (C2, G1, and_12_out, and_14_out);
  or or_4 (G, g0_t, g1_t, g2_t, G3);
  and and_13 (G0, a0, b0);
  and and_14 (and_14_out, P1, P0, Carry_in);
  xor xor_7 (P0, a0, b0);
  xor xor_8 (s0, P0, Carry_in);
  or or_5 (C1, G0, and_15_out);
  and and_15 (and_15_out, P0, Carry_in);
endmodule

module second_level_CLA (
  input  p3,
  input  g3,
  input  p2,
  input  g2,
  input  p1,
  input  g1,
  input  p0,
  input  g0,
  output s3,
  output s2,
  output s1,
  output Carry_out,
  output G,
  output P
);

  wire and_6_out, and_8_out, and_9_out, and_11_out, and_12_out, and_14_out, and_15_out, C1, C2, C3, G0_t,
       g0_t_t, G1_t, g1_t_t, G2_t, g2_t_t, G3_t, P0_t, P1_t, P2_t, P3_t;

  and and_1 (G3_t, p3, g3);
  and and_2 (g1_t_t, P3_t, P2_t, G1_t);
  and and_3 (g2_t_t, P3_t, G2_t);
  or or_1 (Carry_out, G3_t, g2_t_t, g1_t_t, g0_t_t, and_6_out);
  xor xor_1 (P3_t, p3, g3);
  and and_4 (g0_t_t, P3_t, P2_t, P1_t, G0_t);
  and and_5 (G2_t, p2, g2);
  xor xor_2 (s3, P3_t, C3);
  and and_6 (and_6_out, P3_t, P2_t, P1_t, P0_t);
  and and_7 (P, P0_t, P1_t, P2_t, P3_t);
  xor xor_3 (P2_t, p2, g2);
  and and_8 (and_8_out, P2_t, G1_t);
  and and_9 (and_9_out, P2_t, P1_t, G0_t);
  or or_2 (C3, G2_t, and_8_out, and_9_out, and_11_out);
  and and_10 (G1_t, p1, g1);
  xor xor_4 (s2, P2_t, C2);
  and and_11 (and_11_out, P2_t, P1_t, P0_t);
  xor xor_5 (P1_t, p1, g1);
  xor xor_6 (s1, P1_t, C1);
  and and_12 (and_12_out, P1_t, G0_t);
  or or_3 (C2, G1_t, and_12_out, and_14_out);
  or or_4 (G, g0_t_t, g1_t_t, g2_t_t, G3_t);
  and and_13 (G0_t, p0, g0);
  and and_14 (and_14_out, P1_t, P0_t);
  xor xor_7 (P0_t, p0, g0);
  or or_5 (C1, G0_t, and_15_out);
  buf and_15 (and_15_out, P0_t);  // AND_Gate
endmodule

module _16bit_adder_extension (
  input  a15,
  input  a14,
  input  a13,
  input  a12,
  input  a11,
  input  a10,
  input  a9,
  input  a8,
  input  a7,
  input  a6,
  input  a5,
  input  a4,
  input  a3,
  input  a2,
  input  a1,
  input  a0,
  input  in_17,
  input  in_18,
  input  in_19,
  input  b12,
  input  in_21,
  input  in_22,
  input  in_23,
  input  b8,
  input  in_25,
  input  in_26,
  input  in_27,
  input  b4,
  input  in_29,
  input  in_30,
  input  in_31,
  input  b0,
  input  Carry_in,
  output s15,
  output s14,
  output s13,
  output s12,
  output s11,
  output s10,
  output s9,
  output s8,
  output s7,
  output s6,
  output s5,
  output s4,
  output s3,
  output s2,
  output s1,
  output s0,
  output G,
  output P,
  output Overflow
);

  wire C1, C2, C3, G0, G1, G2, G3, P0, P1, P2, P3, second_level_cla_1_carry_out;

  carry_lookahead_extension carry_lookahead_extension_1 (
    .a3(a15), .b3(in_17), .a2(a14), .b2(in_18), .a1(a13), .b1(in_19), .a0(a12), .b0(b12), .Carry_in(C3),
    .s3(s15), .s2(s14), .s1(s13), .s0(s12), .G(G3), .P(P3));  // open: Carry_out
  xor xor_1 (Overflow, second_level_cla_1_carry_out, C3);
  carry_lookahead_extension carry_lookahead_extension_2 (
    .a3(a11), .b3(in_21), .a2(a10), .b2(in_22), .a1(a9), .b1(in_23), .a0(a8), .b0(b8), .Carry_in(C2),
    .s3(s11), .s2(s10), .s1(s9), .s0(s8), .G(G2), .P(P2));  // open: Carry_out
  second_level_CLA second_level_cla_1 (
    .p3(P3), .g3(G3), .p2(P2), .g2(G2), .p1(P1), .g1(G1), .p0(P0), .g0(G0),
    .Carry_out(second_level_cla_1_carry_out), .s3(C3), .s2(C2), .s1(C1), .G(G), .P(P));
  carry_lookahead_extension carry_lookahead_extension_3 (
    .a3(a7), .b3(in_25), .a2(a6), .b2(in_26), .a1(a5), .b1(in_27), .a0(a4), .b0(b4), .Carry_in(C1), .s3(s7),
    .s2(s6), .s1(s5), .s0(s4), .G(G1), .P(P1));  // open: Carry_out
  carry_lookahead_extension carry_lookahead_extension_4 (
    .a3(a3), .b3(in_29), .a2(a2), .b2(in_30), .a1(a1), .b1(in_31), .a0(a0), .b0(b0), .Carry_in(Carry_in),
    .s3(s3), .s2(s2), .s1(s1), .s0(s0), .G(G0), .P(P0));  // open: Carry_out
endmodule

module _16bit_Add_Subtract (
  input  Addend_B,
  input  in_2,
  input  in_3,
  input  in_4,
  input  in_5,
  input  in_6,
  input  in_7,
  input  in_8,
  input  in_9,
  input  in_10,
  input  in_11,
  input  in_12,
  input  in_13,
  input  in_14,
  input  in_15,
  input  in_16,
  input  Add_signal,
  input  Addend_A,
  input  in_19,
  input  in_20,
  input  in_21,
  input  in_22,
  input  in_23,
  input  in_24,
  input  in_25,
  input  in_26,
  input  in_27,
  input  in_28,
  input  in_29,
  input  in_30,
  input  in_31,
  input  in_32,
  input  in_33,
  output overflow,
  output s15,
  output s14,
  output s13,
  output s12,
  output s11,
  output s10,
  output s9,
  output s8,
  output s7,
  output s6,
  output s5,
  output s4,
  output s3,
  output s2,
  output s1,
  output s0
);

  wire not_1_out, xor_1_out, xor_2_out, xor_3_out, xor_4_out, xor_5_out, xor_6_out, xor_7_out, xor_8_out,
       xor_9_out, xor_10_out, xor_11_out, xor_12_out, xor_13_out, xor_14_out, xor_15_out, xor_16_out;

  xor xor_1 (xor_1_out, not_1_out, Addend_B);
  xor xor_2 (xor_2_out, not_1_out, in_2);
  xor xor_3 (xor_3_out, not_1_out, in_3);
  xor xor_4 (xor_4_out, not_1_out, in_5);
  xor xor_5 (xor_5_out, not_1_out, in_4);
  xor xor_6 (xor_6_out, not_1_out, in_8);
  xor xor_7 (xor_7_out, not_1_out, in_6);
  xor xor_8 (xor_8_out, not_1_out, in_7);
  xor xor_9 (xor_9_out, not_1_out, in_10);
  xor xor_10 (xor_10_out, not_1_out, in_9);
  xor xor_11 (xor_11_out, not_1_out, in_13);
  xor xor_12 (xor_12_out, not_1_out, in_11);
  xor xor_13 (xor_13_out, not_1_out, in_12);
  xor xor_14 (xor_14_out, not_1_out, in_14);
  xor xor_15 (xor_15_out, not_1_out, in_15);
  xor xor_16 (xor_16_out, not_1_out, in_16);
  _16bit_adder_with_overflow u_16bit_adder_with_overflow_1 (
    .carry_in(not_1_out), .a15(Addend_A), .b15(xor_1_out), .a14(in_19), .b14(xor_2_out), .a13(in_20),
    .b13(xor_3_out), .a12(in_21), .b12(xor_5_out), .a11(in_22), .b11(xor_4_out), .a10(in_23),
    .b10(xor_7_out), .a9(in_24), .b9(xor_8_out), .a8(in_25), .b8(xor_6_out), .a7(in_26), .b7(xor_10_out),
    .a6(in_27), .b6(xor_9_out), .a5(in_28), .b5(xor_12_out), .a4(in_29), .b4(xor_13_out), .a3(in_30),
    .b3(xor_11_out), .a2(in_31), .b2(xor_14_out), .a1(in_32), .b1(xor_15_out), .a0(in_33), .b0(xor_16_out),
    .Overflow(s15), .s15(overflow), .s14(s14), .s13(s13), .s12(s12), .s11(s11), .s10(s10), .s9(s9), .s8(s8),
    .s7(s7), .s6(s6), .s5(s5), .s4(s4), .s3(s3), .s2(s2), .s1(s1), .s0(s0));
  not not_1 (not_1_out, Add_signal);
endmodule
