// Logisim project 6-instruction-processor+SKELETON.circ as structural Verilog: 6 circuits, main circuit 32-bit ALU
module datapath (
  input  Start
);

  wire Add_p5, CLK, Decode_p3, Decode_p5, Decode_p6, Decode_p7, Decode_p8, Decode_p9, EqZero, Fetch_p3,
       Fetch_p8, Fetch_p11, Fetch_p12, Init_p3, Init_p5, IR_CLR, IR_LD, JumpIfZero, JumpJump_p4, JumpJump_p5,
       Load_Constant_p5, Load_p5, PC_LD, Read_En_A, Read_En_B, Read_Mem, Store_p5, Subtract_p5, ToFetch,
       ToFetch2, ToFetch3, ToFetch4, ToFetch5, Wr_Mem;
  wire [1:0] Reg_Input_Select;
  wire [2:0] ALU_Select, OP_CODE, Read_Addr_A, Read_Addr_B, RegA, Wr_Addr;
  wire [7:0] adder_1_out, Constant, counter_1_q, MemAddress, subtractor_1_out;
  wire [15:0] rom_1_data;
  wire [15:11] IR_q;
  wire [31:0] multiplexer_1_out, n32_bit_alu_1_sum, ram_1_data, registerfile_1_read_dataa,
       registerfile_1_read_datab;

  Clock clock_1 (.out(CLK));
  Adder adder_1 (.a(counter_1_q), .b(subtractor_1_out), .out(adder_1_out));  // open: cin, cout
  Subtractor subtractor_1 (.a(Constant), .b(8'h1), .out(subtractor_1_out));  // open: bin, bout
  // StateMachine Init: pin names not known; wires that end beside it: CLK, 1'b0, Init_p3, Start, Init_p5
  Pull_Resistor pull_resistor_1 (.node(Read_Mem));
  Pull_Resistor pull_resistor_2 (.node(Read_En_A));
  Pull_Resistor pull_resistor_3 (.node(Read_En_B));
  Pull_Resistor pull_resistor_4 (.node(Wr_Mem));
  Pull_Resistor pull_resistor_5 (.node(Read_Mem));
  Pull_Resistor pull_resistor_6 (.node(PC_LD));
  Pull_Resistor pull_resistor_7 (.node(IR_LD));
  Pull_Resistor pull_resistor_8 (.node(IR_CLR));
  Pull_Resistor pull_resistor_9 (.node(IR_LD));
  Pull_Resistor pull_resistor_10 (.node(IR_CLR));
  Counter counter_1 (
    .load(PC_LD), .D(adder_1_out), .count(IR_LD), .Q(counter_1_q), .clk(CLK), .clr(IR_CLR));  // open: carry
  assign IR_CLR = Init_p5 ? 1'b1 : 1'bz;  // Controlled_Buffer controlled_buffer_1
  // StateMachine Fetch: pin names not known; wires that end beside it: CLK, 1'b0, Fetch_p3, ToFetch, ToFetch2, ToFetch3, ToFetch5, Fetch_p8, ToFetch4, Init_p3, Fetch_p11, Fetch_p12
  ROM #(.dataWidth(16)) rom_1 (.addr(counter_1_q), .data(rom_1_data));  // open: sel
  Register #(.width(16)) IR (
    .D(rom_1_data), .en(IR_LD), .Q({IR_q[15], OP_CODE, IR_q[11], RegA, Constant}), .clk(CLK), .clr(IR_CLR));
  assign IR_LD = Fetch_p12 ? 1'b1 : 1'bz;  // Controlled_Buffer controlled_buffer_2
  // StateMachine JumpJump: pin names not known; wires that end beside it: CLK, 1'b0, Fetch_p8, JumpJump_p4, JumpJump_p5
  // Probe on rom_1_data
  // Probe on {IR_q[11], RegA, Constant}
  // Probe on OP_CODE
  // StateMachine #(.select(3)) Decode: pin names not known; wires that end beside it: CLK, OP_CODE, Decode_p3, Fetch_p3, Decode_p5, Decode_p6, Decode_p7, Decode_p8, Decode_p9
  // StateMachine JumpIfZero: pin names not known; wires that end beside it: CLK, EqZero, Fetch_p11, Decode_p9, JumpJump_p4, JumpIfZero
  assign PC_LD = JumpJump_p5 ? 1'b1 : 1'bz;  // Controlled_Buffer controlled_buffer_3
  assign Read_Addr_A = JumpIfZero ? RegA : 3'bz;  // Controlled_Buffer controlled_buffer_4
  assign Read_En_A = JumpIfZero ? 1'b1 : 1'bz;  // Controlled_Buffer controlled_buffer_5
  // StateMachine Add: pin names not known; wires that end beside it: CLK, 1'b0, ToFetch, Decode_p6, Add_p5
  assign Read_En_B = Add_p5 ? 1'b1 : 1'bz;  // Controlled_Buffer controlled_buffer_6
  // StateMachine Subtract: pin names not known; wires that end beside it: CLK, 1'b0, ToFetch4, Decode_p8, Subtract_p5
  Comparator #(.width(32)) comparator_1 (.a(registerfile_1_read_dataa), .b({32{1'b0}}), .eq(EqZero));  // open: gt, lt
  assign Read_Mem = Add_p5 ? 1'b1 : 1'bz;  // Controlled_Buffer controlled_buffer_7
  assign Wr_Addr = Add_p5 ? RegA : 3'bz;  // Controlled_Buffer controlled_buffer_8
  assign Read_Addr_A = Add_p5 ? Constant[6:4] : 3'bz;  // Controlled_Buffer controlled_buffer_9
  assign Read_Addr_B = Add_p5 ? Constant[2:0] : 3'bz;  // Controlled_Buffer controlled_buffer_10
  assign ALU_Select = Add_p5 ? 3'b001 : 3'bz;  // Controlled_Buffer controlled_buffer_11
  assign Reg_Input_Select = Add_p5 ? 2'b01 : 2'bz;  // Controlled_Buffer controlled_buffer_12
  assign Read_Mem = Subtract_p5 ? 1'b1 : 1'bz;  // Controlled_Buffer controlled_buffer_13
  assign ALU_Select = Subtract_p5 ? 3'b000 : 3'bz;  // Controlled_Buffer controlled_buffer_14
  assign Reg_Input_Select = Subtract_p5 ? 2'b01 : 2'bz;  // Controlled_Buffer controlled_buffer_15
  assign Read_En_B = Subtract_p5 ? 1'b1 : 1'bz;  // Controlled_Buffer controlled_buffer_16
  assign Read_En_A = Add_p5 ? 1'b1 : 1'bz;  // Controlled_Buffer controlled_buffer_17
  assign Wr_Addr = Subtract_p5 ? RegA : 3'bz;  // Controlled_Buffer controlled_buffer_18
  assign Read_Addr_A = Subtract_p5 ? Constant[6:4] : 3'bz;  // Controlled_Buffer controlled_buffer_19
  assign Read_Addr_B = Subtract_p5 ? Constant[2:0] : 3'bz;  // Controlled_Buffer controlled_buffer_20
  assign Read_En_A = Subtract_p5 ? 1'b1 : 1'bz;  // Controlled_Buffer controlled_buffer_21
  Multiplexer #(.select(2), .width(32), .disabled(0), .enable("false")) multiplexer_1 (
    .in0(ram_1_data), .in1(n32_bit_alu_1_sum), .in2({{24{1'b0}}, Constant}), .out(multiplexer_1_out),
    .sel(Reg_Input_Select));  // open: in3
  RegisterFile registerfile_1 (
    .Clock(CLK), .Write_Address(Wr_Addr), .Write_Enable(Read_Mem), .Read_AddressA(Read_Addr_A),
    .Read_EnableA(Read_En_A), .Read_AddressB(Read_Addr_B), .Read_EnableB(Read_En_B),
    .Write_Data(multiplexer_1_out), .Read_DataA(registerfile_1_read_dataa),
    .Read_DataB(registerfile_1_read_datab));
  _32_bit_ALU u_32_bit_alu_1 (
    .Select(ALU_Select), .A(registerfile_1_read_dataa), .B(registerfile_1_read_datab), .SUM(n32_bit_alu_1_sum));  // open: CARRY_OUT
  RAM #(.dataWidth(32), .bus("separate")) ram_1 (
    .addr(MemAddress), .din(registerfile_1_read_dataa), .data(ram_1_data), .str(Wr_Mem), .clk(CLK),
    .ld(Read_Mem));  // open: sel, clr
  // StateMachine Load: pin names not known; wires that end beside it: CLK, 1'b0, ToFetch2, Decode_p3, Load_p5
  // StateMachine Store: pin names not known; wires that end beside it: CLK, 1'b0, ToFetch3, Decode_p5, Store_p5
  // StateMachine Load_Constant: pin names not known; wires that end beside it: CLK, 1'b0, ToFetch5, Decode_p7, Load_Constant_p5
  assign Reg_Input_Select = Load_p5 ? 2'b00 : 2'bz;  // Controlled_Buffer controlled_buffer_22
  assign Wr_Addr = Load_p5 ? RegA : 3'bz;  // Controlled_Buffer controlled_buffer_23
  assign Read_Mem = Load_p5 ? 1'b1 : 1'bz;  // Controlled_Buffer controlled_buffer_24
  assign MemAddress = Load_p5 ? Constant : 8'bz;  // Controlled_Buffer controlled_buffer_25
  assign Read_Addr_A = Store_p5 ? RegA : 3'bz;  // Controlled_Buffer controlled_buffer_26
  assign Read_En_A = Store_p5 ? 1'b1 : 1'bz;  // Controlled_Buffer controlled_buffer_27
  assign Wr_Mem = Store_p5 ? 1'b1 : 1'bz;  // Controlled_Buffer controlled_buffer_28
  assign MemAddress = Store_p5 ? Constant : 8'bz;  // Controlled_Buffer controlled_buffer_29
  assign Wr_Addr = Load_Constant_p5 ? RegA : 3'bz;  // Controlled_Buffer controlled_buffer_30
  assign Reg_Input_Select = Load_Constant_p5 ? 2'b10 : 2'bz;  // Controlled_Buffer controlled_buffer_31
  assign Read_Mem = Load_Constant_p5 ? 1'b1 : 1'bz;  // Controlled_Buffer controlled_buffer_32

  // Other names for the same wires on the sheet: MemAddressD[7:0] = Constant; Offset[7:0] = Constant;
  //   RegC[2:0] = Constant[2:0]; RegB[2:0] = Constant[6:4]; RegD[2:0] = RegA; PC_CLR = IR_CLR; PC_INC = IR_LD;
  //   W_En = Read_Mem

  // Notes on the sheet:
  //   This program is from fig 8.14 in the text
  //   contents of rom_1 (hex, n*v repeats v):
  //   3000 3101 204 5202 2001 205 5202 2001 1009
  //   Fill in outputs for this state
  //   Fill in outputs for this state
  //   Write some values in locations 4, 5, 6 to vary the operation of the program
  //   these red lines are OK when it's running
  //   Fill in outputs for this state
endmodule

module _32_bit_ALU (
  input  [2:0] Select,
  input  [31:0] A,
  input  [31:0] B,
  output CARRY_OUT,
  output [31:0] SUM
);

  wire multiplexer_3_out;
  wire [31:0] A___8, A___8_t, A_NAND_B, A_XOR_B, multiplexer_1_out, multiplexer_2_out, NOT_A, NOT_B,
       REVERSE_A;

  Shifter #(.width(32)) shifter_1 (.in(A), .\dist (5'b00011), .out(A___8));
  assign A_XOR_B = A ^ B;  // XOR_Gate A_XOR_B, 32 bits wide
  assign A_NAND_B = ~(A & B);  // NAND_Gate A_NAND_B, 32 bits wide
  Multiplexer #(.select(3), .width(32), .disabled(0), .enable("false")) multiplexer_1 (
    .in0(A), .in1(A), .in2(A___8), .in3(A___8_t), .in4(A_NAND_B), .in5(A_XOR_B), .in6(REVERSE_A),
    .in7(NOT_A), .out(multiplexer_1_out), .sel(Select));
  assign NOT_A = ~A;  // NOT_Gate NOT_A, 32 bits wide
  Shifter #(.width(32), .shift("lr")) shifter_2 (.in(A), .\dist (5'b00011), .out(A___8_t));
  assign NOT_B = ~B;  // NOT_Gate NOT_B, 32 bits wide
  Adder #(.width(32)) adder_1 (
    .a(multiplexer_1_out), .b(multiplexer_2_out), .out(SUM), .cin(multiplexer_3_out), .cout(CARRY_OUT));
  REVERSE_A u_REVERSE_A (.A(A), .REVERSE_A(REVERSE_A));
  Multiplexer #(.select(3), .width(32), .disabled(0), .enable("false")) multiplexer_2 (
    .in0(NOT_B), .in1(B), .in2({32{1'b0}}), .in3({32{1'b0}}), .in4({32{1'b0}}), .in5({32{1'b0}}),
    .in6({32{1'b0}}), .in7({32{1'b0}}), .out(multiplexer_2_out), .sel(Select));
  Multiplexer #(.select(3), .disabled(0), .enable("false")) multiplexer_3 (
    .in0(1'b1), .in1(1'b0), .in2(1'b0), .in3(1'b0), .in4(1'b0), .in5(1'b0), .in6(1'b0), .in7(1'b0),
    .out(multiplexer_3_out), .sel(Select));

  // Notes on the sheet:
  //   Adapted from ALU design by Joshua Storer December 2011
endmodule

module REVERSE_A (
  input  [31:0] A,
  output [31:0] REVERSE_A
);


  assign REVERSE_A = {A[0], A[1], A[2], A[3], A[4], A[5], A[6], A[7], A[8], A[9], A[10], A[11], A[12], A[13], A[14], A[15], A[16], A[17], A[18], A[19], A[20], A[21], A[22], A[23], A[24], A[25], A[26], A[27], A[28], A[29], A[30], A[31]};
endmodule

module RegisterFile (
  input  [31:0] Write_Data,
  input  Clock,
  input  [2:0] Write_Address,
  input  Write_Enable,
  input  [2:0] Read_AddressA,
  input  Read_EnableA,
  input  [2:0] Read_AddressB,
  input  Read_EnableB,
  output [31:0] Read_DataB,
  output [31:0] Read_DataA
);

  wire decoder_1_out0, decoder_1_out1, decoder_1_out2, decoder_1_out3, decoder_1_out4, decoder_1_out5,
       decoder_1_out6, decoder_1_out7, decoder_2_out0, decoder_2_out1, decoder_2_out2, decoder_2_out3,
       decoder_2_out4, decoder_2_out5, decoder_2_out6, decoder_2_out7, decoder_3_out0, decoder_3_out1,
       decoder_3_out2, decoder_3_out3, decoder_3_out4, decoder_3_out5, decoder_3_out6, decoder_3_out7;
  wire [31:0] register_1_q, register_2_q, register_3_q, register_4_q, register_5_q, register_6_q,
       register_7_q, register_8_q;

  Decoder #(.select(3), .disabled(0)) decoder_1 (
    .out0(decoder_1_out0), .out1(decoder_1_out1), .out2(decoder_1_out2), .out3(decoder_1_out3),
    .out4(decoder_1_out4), .out5(decoder_1_out5), .out6(decoder_1_out6), .out7(decoder_1_out7),
    .sel(Write_Address), .en(Write_Enable));
  Register #(.width(32)) register_1 (.D(Write_Data), .en(decoder_1_out7), .Q(register_1_q), .clk(Clock));  // open: clr
  Register #(.width(32)) register_2 (.D(Write_Data), .en(decoder_1_out6), .Q(register_2_q), .clk(Clock));  // open: clr
  Register #(.width(32)) register_3 (.D(Write_Data), .en(decoder_1_out5), .Q(register_3_q), .clk(Clock));  // open: clr
  Register #(.width(32)) register_4 (.D(Write_Data), .en(decoder_1_out4), .Q(register_4_q), .clk(Clock));  // open: clr
  Register #(.width(32)) register_5 (.D(Write_Data), .en(decoder_1_out3), .Q(register_5_q), .clk(Clock));  // open: clr
  Register #(.width(32)) register_6 (.D(Write_Data), .en(decoder_1_out2), .Q(register_6_q), .clk(Clock));  // open: clr
  Register #(.width(32)) register_7 (.D(Write_Data), .en(decoder_1_out1), .Q(register_7_q), .clk(Clock));  // open: clr
  Register #(.width(32)) register_8 (.D(Write_Data), .en(decoder_1_out0), .Q(register_8_q), .clk(Clock));  // open: clr
  Decoder #(.select(3), .disabled(0)) decoder_2 (
    .out0(decoder_2_out0), .out1(decoder_2_out1), .out2(decoder_2_out2), .out3(decoder_2_out3),
    .out4(decoder_2_out4), .out5(decoder_2_out5), .out6(decoder_2_out6), .out7(decoder_2_out7),
    .sel(Read_AddressA), .en(Read_EnableA));
  assign Read_DataA = decoder_2_out7 ? register_1_q : 32'bz;  // Controlled_Buffer controlled_buffer_1
  assign Read_DataA = decoder_2_out6 ? register_2_q : 32'bz;  // Controlled_Buffer controlled_buffer_2
  assign Read_DataA = decoder_2_out5 ? register_3_q : 32'bz;  // Controlled_Buffer controlled_buffer_3
  assign Read_DataA = decoder_2_out4 ? register_4_q : 32'bz;  // Controlled_Buffer controlled_buffer_4
  assign Read_DataA = decoder_2_out3 ? register_5_q : 32'bz;  // Controlled_Buffer controlled_buffer_5
  assign Read_DataA = decoder_2_out2 ? register_6_q : 32'bz;  // Controlled_Buffer controlled_buffer_6
  assign Read_DataA = decoder_2_out1 ? register_7_q : 32'bz;  // Controlled_Buffer controlled_buffer_7
  assign Read_DataA = decoder_2_out0 ? register_8_q : 32'bz;  // Controlled_Buffer controlled_buffer_8
  assign Read_DataB = decoder_3_out7 ? register_1_q : 32'bz;  // Controlled_Buffer controlled_buffer_9
  assign Read_DataB = decoder_3_out6 ? register_2_q : 32'bz;  // Controlled_Buffer controlled_buffer_10
  assign Read_DataB = decoder_3_out5 ? register_3_q : 32'bz;  // Controlled_Buffer controlled_buffer_11
  assign Read_DataB = decoder_3_out4 ? register_4_q : 32'bz;  // Controlled_Buffer controlled_buffer_12
  assign Read_DataB = decoder_3_out3 ? register_5_q : 32'bz;  // Controlled_Buffer controlled_buffer_13
  assign Read_DataB = decoder_3_out2 ? register_6_q : 32'bz;  // Controlled_Buffer controlled_buffer_14
  assign Read_DataB = decoder_3_out1 ? register_7_q : 32'bz;  // Controlled_Buffer controlled_buffer_15
  assign Read_DataB = decoder_3_out0 ? register_8_q : 32'bz;  // Controlled_Buffer controlled_buffer_16
  Decoder #(.select(3), .disabled(0)) decoder_3 (
    .out0(decoder_3_out0), .out1(decoder_3_out1), .out2(decoder_3_out2), .out3(decoder_3_out3),
    .out4(decoder_3_out4), .out5(decoder_3_out5), .out6(decoder_3_out6), .out7(decoder_3_out7),
    .sel(Read_AddressB), .en(Read_EnableB));
endmodule

module instruction (
);

  wire CLK, IR_CLR, IR_LD, PC_CLR, PC_INC, PC_LD;
  wire [2:0] OP_CODE, RegA;
  wire [7:0] adder_1_out, Constant, counter_1_q, subtractor_1_out;
  wire [15:0] rom_1_data;
  wire [15:11] IR_q;

  Adder adder_1 (.a(counter_1_q), .b(subtractor_1_out), .out(adder_1_out));  // open: cin, cout
  Subtractor subtractor_1 (.a(Constant), .b(8'h1), .out(subtractor_1_out));  // open: bin, bout
  Counter counter_1 (
    .load(PC_LD), .D(adder_1_out), .count(PC_INC), .Q(counter_1_q), .clk(CLK), .clr(PC_CLR));  // open: carry
  ROM #(.dataWidth(16)) rom_1 (.addr(counter_1_q), .data(rom_1_data));  // open: sel
  Register #(.width(16)) IR (
    .D(rom_1_data), .en(IR_LD), .Q({IR_q[15], OP_CODE, IR_q[11], RegA, Constant}), .clk(CLK), .clr(IR_CLR));

  // Other names for the same wires on the sheet: MemAddressD[7:0] = Constant; Offset[7:0] = Constant;
  //   RegC[2:0] = Constant[2:0]; RegB[2:0] = Constant[6:4]; RegD[2:0] = RegA

  // Notes on the sheet:
  //   contents of rom_1 (hex, n*v repeats v):
  //   3000 3101 204 5202 2001 205 5202 2001 1009
endmodule

module datapath_separate (
);

  wire CLK, EqZero, Read_En_A, Read_En_B, Read_Mem, W_En, Wr_Mem;
  wire [1:0] Reg_Input_Select;
  wire [2:0] ALU_select, Read_Addr_A, Read_Addr_B, Wr_Addr;
  wire [7:0] MemAddress;
  wire [31:0] Constant, multiplexer_1_out, n32_bit_alu_1_sum, ram_1_data, registerfile_1_read_dataa,
       registerfile_1_read_datab;

  Comparator #(.width(32)) comparator_1 (.a(registerfile_1_read_dataa), .b({32{1'b0}}), .eq(EqZero));  // open: gt, lt
  Pull_Resistor pull_resistor_1 (.node(Wr_Mem));
  Pull_Resistor pull_resistor_2 (.node(Read_Mem));
  Multiplexer #(.select(2), .width(32), .disabled(0), .enable("false")) multiplexer_1 (
    .in0(ram_1_data), .in1(n32_bit_alu_1_sum), .in2(Constant), .out(multiplexer_1_out), .sel(Reg_Input_Select));  // open: in3
  RegisterFile registerfile_1 (
    .Clock(CLK), .Write_Address(Wr_Addr), .Write_Enable(W_En), .Read_AddressA(Read_Addr_A),
    .Read_EnableA(Read_En_A), .Read_AddressB(Read_Addr_B), .Read_EnableB(Read_En_B),
    .Write_Data(multiplexer_1_out), .Read_DataA(registerfile_1_read_dataa),
    .Read_DataB(registerfile_1_read_datab));
  _32_bit_ALU u_32_bit_alu_1 (
    .Select(ALU_select), .A(registerfile_1_read_dataa), .B(registerfile_1_read_datab), .SUM(n32_bit_alu_1_sum));  // open: CARRY_OUT
  RAM #(.dataWidth(32), .bus("separate")) ram_1 (
    .addr(MemAddress), .din(registerfile_1_read_dataa), .data(ram_1_data), .str(Wr_Mem), .clk(CLK),
    .ld(Read_Mem));  // open: sel, clr
endmodule
