// Logisim project LAB_2.circ as structural Verilog: 2 circuits, main circuit UVA
module UVA (
  input  [2:0] in_1,
  output Entrance
);

  or or_1 (Entrance, in_1[0], in_1[2]);

  // Other names for the same wires on the sheet: young = in_1[0]; ODD = in_1[1]; SEAS = in_1[2]
endmodule

module clown (
  input  [2:0] in_1,
  output Entrance
);

  wire not_1_out;

  not not_1 (not_1_out, in_1[0]);
  or or_1 (Entrance, not_1_out, in_1[2]);

  // Other names for the same wires on the sheet: mine = in_1[0]; juggle = in_1[1]; tumble = in_1[2]
endmodule
