// Logisim project Studio+Nand+Nor+Skeleton.circ as structural Verilog: 5 circuits, main circuit AND/OR
module AND_OR (
  input  A,
  input  B,
  input  C,
  input  D,
  output F1
);

  wire and_1_out, and_2_out, and_3_out, not_1_out, not_2_out, not_3_out, not_4_out;

  not not_1 (not_1_out, A);
  not not_2 (not_2_out, B);
  not not_3 (not_3_out, C);
  not not_4 (not_4_out, D);
  and and_1 (and_1_out, not_2_out, not_4_out);
  and and_2 (and_2_out, A, B, C);
  and and_3 (and_3_out, not_1_out, B, not_3_out);
  or or_1 (F1, and_1_out, and_2_out, and_3_out);
endmodule

module NAND_only (
  input  A,
  input  B,
  input  C,
  input  D,
  output F2
);

  wire nand_1_out, nand_2_out, nand_3_out, not_1_out, not_2_out, not_3_out, not_4_out;

  not not_1 (not_1_out, A);
  not not_2 (not_2_out, C);
  not not_3 (not_3_out, B);
  not not_4 (not_4_out, D);
  nand nand_1 (nand_1_out, not_3_out, not_4_out);
  nand nand_2 (nand_2_out, A, B, C);
  nand nand_3 (nand_3_out, not_1_out, B, not_2_out);
  nand nand_4 (F2, nand_1_out, nand_2_out, nand_3_out);
endmodule

module OR_AND (
  input  A,
  input  B,
  input  C,
  input  D,
  output F3
);

  wire not_1_out, not_2_out, not_3_out, not_4_out, or_1_out, or_2_out, or_3_out;

  not not_1 (not_1_out, A);
  not not_2 (not_2_out, B);
  not not_3 (not_3_out, C);
  not not_4 (not_4_out, D);
  or or_1 (or_1_out, B, not_4_out);
  or or_2 (or_2_out, not_1_out, not_2_out, C);
  or or_3 (or_3_out, A, not_2_out, not_3_out);
  and and_1 (F3, or_1_out, or_2_out, or_3_out);
endmodule

module NOR_only (
  input  A,
  input  B,
  input  C,
  input  D,
  output out_5
);

  wire nor_1_out, nor_2_out, nor_3_out, not_1_out, not_2_out, not_3_out, not_4_out;

  not not_1 (not_1_out, A);
  not not_2 (not_2_out, C);
  not not_3 (not_3_out, B);
  not not_4 (not_4_out, D);
  nor nor_1 (nor_1_out, B, not_4_out);
  nor nor_2 (nor_2_out, not_1_out, not_3_out, C);
  nor nor_3 (nor_3_out, A, not_3_out, not_2_out);
  nor nor_4 (out_5, nor_1_out, nor_2_out, nor_3_out);
endmodule

module all_four_together (
  output F1__AND_OR,
  output F2__NAND_only,
  output F3__OR_AND,
  output F4__NOR_only
);

  wire and_1_out, and_2_out, and_3_out, clock_1_out, nand_1_out, nand_2_out, nand_3_out, nor_1_out,
       nor_2_out, nor_3_out, not_1_out, not_2_out, not_3_out, not_4_out, or_1_out, or_2_out, or_3_out;
  wire [3:0] counter_1_q;

  Counter #(.width(4), .max('hf)) counter_1 (
    .count(1'b1), .Q(counter_1_q), .clk(clock_1_out));  // open: load, D, carry, clr
  Clock clock_1 (.out(clock_1_out));
  not not_1 (not_1_out, counter_1_q[2]);
  not not_2 (not_2_out, counter_1_q[1]);
  not not_3 (not_3_out, counter_1_q[3]);
  not not_4 (not_4_out, counter_1_q[0]);
  and and_1 (and_1_out, not_1_out, not_4_out);
  and and_2 (and_2_out, counter_1_q[3], counter_1_q[2], counter_1_q[1]);
  and and_3 (and_3_out, not_3_out, counter_1_q[2], not_2_out);
  nand nand_1 (nand_1_out, not_1_out, not_4_out);
  nand nand_2 (nand_2_out, counter_1_q[3], counter_1_q[2], counter_1_q[1]);
  nand nand_3 (nand_3_out, not_3_out, counter_1_q[2], not_2_out);
  or or_1 (or_1_out, counter_1_q[2], not_4_out);
  or or_2 (or_2_out, not_3_out, not_1_out, counter_1_q[1]);
  or or_3 (or_3_out, counter_1_q[3], not_1_out, not_2_out);
  nor nor_1 (nor_1_out, counter_1_q[2], not_4_out);
  nor nor_2 (nor_2_out, not_3_out, not_1_out, counter_1_q[1]);
  nor nor_3 (nor_3_out, counter_1_q[3], not_1_out, not_2_out);
  or or_4 (F1__AND_OR, and_1_out, and_2_out, and_3_out);
  nand nand_4 (F2__NAND_only, nand_1_out, nand_2_out, nand_3_out);
  and and_4 (F3__OR_AND, or_1_out, or_2_out, or_3_out);
  nor nor_4 (F4__NOR_only, nor_1_out, nor_2_out, nor_3_out);
endmodule
