// Logisim project MUX.CIR.circ as structural Verilog: 4 circuits, main circuit Mux
module Mux (
  input  in_1,
  input  in_2,
  input  in_3,
  input  in_4,
  input  [1:0] S1_S0,
  output Output
);

  wire decoder_1_out0, decoder_1_out1, decoder_1_out2, decoder_1_out3, nand_1_out, nand_2_out, nand_3_out,
       nand_4_out;

  Decoder #(.select(2), .disabled(0), .enable("false")) decoder_1 (
    .out0(decoder_1_out0), .out1(decoder_1_out1), .out2(decoder_1_out2), .out3(decoder_1_out3), .sel(S1_S0));
  nand nand_1 (nand_1_out, decoder_1_out0, in_1);
  nand nand_2 (nand_2_out, decoder_1_out1, in_2);
  nand nand_3 (nand_3_out, decoder_1_out2, in_3);
  nand nand_4 (nand_4_out, decoder_1_out3, in_4);
  nand nand_5 (Output, nand_1_out, nand_2_out, nand_3_out, nand_4_out);

  // Other names for the same wires on the sheet: X0 = in_1; X1 = in_2; X2 = in_3; X3 = in_4
endmodule

module _4_to_1_mux (
  input  A,
  input  B,
  input  C,
  input  D,
  input  A_2,
  input  B_2,
  input  C_2,
  input  D_2,
  input  [1:0] in_9,
  input  A_3,
  input  B_3,
  input  C_3,
  input  D_3,
  input  A_4,
  input  B_4,
  input  C_4,
  input  D_4,
  output Z0,
  output Z1,
  output Z2,
  output Z3
);

  wire [1:0] S1__S0_t;

  Mux mux_1 (.in_1(A), .in_2(B), .in_3(C), .in_4(D), .S1_S0(S1__S0_t), .Output(Z0));
  Mux mux_2 (.in_1(A_2), .in_2(B_2), .in_3(C_2), .in_4(D_2), .S1_S0(in_9), .Output(Z1));
  Mux mux_3 (.in_1(A_3), .in_2(B_3), .in_3(C_3), .in_4(D_3), .S1_S0(in_9), .Output(Z2));
  Mux mux_4 (.in_1(A_4), .in_2(B_4), .in_3(C_4), .in_4(D_4), .S1_S0(in_9), .Output(Z3));

  // Other names for the same wires on the sheet: S1__S0[1:0] = in_9
endmodule

module _16_to_1_mux (
  input  in_1,
  input  in_2,
  input  in_3,
  input  in_4,
  input  in_5,
  input  in_6,
  input  in_7,
  input  in_8,
  input  in_9,
  input  in_10,
  input  in_11,
  input  in_12,
  input  in_13,
  input  in_14,
  input  in_15,
  input  in_16,
  input  in_17,
  input  [1:0] in_18,
  output Output
);

  wire decoder_1_out0, decoder_1_out1, multiplexer_1_out, multiplexer_2_out, mux_1_output, mux_2_output,
       mux_3_output, mux_4_output, nand_1_out, nand_2_out;

  Decoder #(.disabled(0), .enable("false")) decoder_1 (.out0(decoder_1_out0), .out1(decoder_1_out1), .sel(in_17));
  Mux mux_1 (.in_1(in_1), .in_2(in_2), .in_3(in_3), .in_4(in_4), .S1_S0(in_18), .Output(mux_1_output));
  Mux mux_2 (.in_1(in_5), .in_2(in_6), .in_3(in_7), .in_4(in_8), .S1_S0(in_18), .Output(mux_2_output));
  Mux mux_3 (.in_1(in_9), .in_2(in_10), .in_3(in_11), .in_4(in_12), .S1_S0(in_18), .Output(mux_3_output));
  Mux mux_4 (.in_1(in_13), .in_2(in_14), .in_3(in_15), .in_4(in_16), .S1_S0(in_18), .Output(mux_4_output));
  Multiplexer #(.enable("false")) multiplexer_1 (
    .in0(mux_1_output), .in1(mux_2_output), .out(multiplexer_1_out), .sel(in_17));
  Multiplexer #(.enable("false")) multiplexer_2 (
    .in0(mux_4_output), .in1(mux_3_output), .out(multiplexer_2_out), .sel(in_17));
  nand nand_1 (nand_1_out, multiplexer_1_out, decoder_1_out0);
  nand nand_2 (nand_2_out, decoder_1_out1, multiplexer_2_out);
  nand nand_3 (Output, nand_1_out, nand_2_out);

  // Other names for the same wires on the sheet: S1__S0[1:0] = in_18; S2 = in_17; X0 = in_1; X1 = in_2; X2 = in_3;
  //   X3 = in_4; X4 = in_5; X5 = in_6; X6 = in_7; X7 = in_8; X8 = in_9; X9 = in_10; X10 = in_11; X11 = in_12;
  //   X12 = in_13; X13 = in_14; X14 = in_15; X15 = in_16
endmodule

module _16_to_1_simplier (
  input  _0,
  input  _1,
  input  _2,
  input  _3,
  input  _4,
  input  _5,
  input  _6,
  input  _7,
  input  [1:0] in_9,
  input  _8,
  input  _9,
  input  [1:0] in_12,
  input  _10,
  input  _11,
  input  _12,
  input  _13,
  input  _14,
  input  _15,
  output out_19
);

  wire mux_1_output, mux_2_output, mux_3_output, mux_4_output;
  wire [1:0] S1__S0_t;

  Mux mux_1 (.in_1(_0), .in_2(_1), .in_3(_2), .in_4(_3), .S1_S0(S1__S0_t), .Output(mux_1_output));
  Mux mux_2 (.in_1(_4), .in_2(_5), .in_3(_6), .in_4(_7), .S1_S0(in_9), .Output(mux_2_output));
  Mux mux_3 (.in_1(_8), .in_2(_9), .in_3(_10), .in_4(_11), .S1_S0(in_9), .Output(mux_3_output));
  Mux mux_4 (.in_1(_12), .in_2(_13), .in_3(_14), .in_4(_15), .S1_S0(in_9), .Output(mux_4_output));
  Mux mux_5 (
    .in_1(mux_1_output), .in_2(mux_2_output), .in_3(mux_3_output), .in_4(mux_4_output), .S1_S0(in_12),
    .Output(out_19));

  // Other names for the same wires on the sheet: S1__S0[1:0] = in_9; S3__S4[1:0] = in_12
endmodule
