// Logisim project mystery+circuits+2.circ as structural Verilog: 7 circuits, main circuit mystery 2 insides
module mystery_1_box (
  input  X7,
  input  X6,
  input  X5,
  input  X4,
  input  X3,
  input  X2,
  input  X1,
  input  X0,
  output Z2,
  output Z1,
  output Z0,
  output R
);

  mystery_1_insides mystery_1_insides_1 (
    .X7(X7), .X6(X6), .X5(X5), .X4(X4), .X3(X3), .X2(X2), .X1(X1), .X0(X0), .Z2(Z2), .Z1(Z1), .Z0(Z0), .R(R));
endmodule

module mystery_1_insides (
  input  X7,
  input  X6,
  input  X5,
  input  X4,
  input  X3,
  input  X2,
  input  X1,
  input  X0,
  output Z2,
  output Z1,
  output Z0,
  output R
);

  or or_1 (Z2, X4, X5, X6, X7);
  or or_2 (Z1, X2, X3, X6, X7);
  or or_3 (Z0, X1, X3, X5, X7);
  or or_4 (R, X0, X1, X2, X3, X4, X5, X6, X7);
endmodule

module mystery_2_box (
  input  X3,
  input  X2,
  input  X1,
  input  X0,
  output R,
  output Z1,
  output Z0
);

  mystery_2_insides mystery_2_insides_1 (.X3(X3), .X2(X2), .X1(X1), .X0(X0), .R(R), .Z1(Z1), .Z0(Z0));
endmodule

module mystery_2_insides (
  input  X3,
  input  X2,
  input  X1,
  input  X0,
  output R,
  output Z1,
  output Z0
);

  wire not_1_out, not_2_out, or_1_out;

  not not_1 (not_1_out, X0);
  not not_2 (not_2_out, X2);
  nor nor_1 (R, X0, X1, X2, X3);
  or or_1 (or_1_out, X1, not_2_out);
  nor nor_2 (Z1, X0, X1);
  and and_1 (Z0, not_1_out, or_1_out);
endmodule

module mystery_2_with_enable (
  input  X3,
  input  X2,
  input  X1,
  input  X0,
  input  E__active_high,
  output R__Active_low,
  output Z1,
  output Z0
);

  wire and_1_out, nor_1_out, not_1_out, not_2_out, or_1_out, or_2_out;

  not not_1 (not_1_out, X0);
  not not_2 (not_2_out, X2);
  or or_1 (or_1_out, X0, X1, X2, X3);
  or or_2 (or_2_out, X1, not_2_out);
  nor nor_1 (nor_1_out, X0, X1);
  and and_1 (and_1_out, not_1_out, or_2_out);
  nand nand_1 (R__Active_low, or_1_out, E__active_high);
  and and_2 (Z1, nor_1_out, E__active_high);
  and and_3 (Z0, and_1_out, E__active_high);
endmodule

module bigger_mystery_2 (
  input  A0,
  input  A1,
  input  A2,
  input  A3,
  input  A4,
  input  Enable,
  input  A5,
  input  A6,
  input  A7,
  output Z2,
  output Z1,
  output Z0,
  output R__Active_low
);

  wire mystery_2_with_enable_1_r__active_low, mystery_2_with_enable_1_z0, mystery_2_with_enable_1_z1,
       mystery_2_with_enable_2_r__active_low, mystery_2_with_enable_2_z0, mystery_2_with_enable_2_z1;

  mystery_2_with_enable mystery_2_with_enable_1 (
    .X3(A3), .X2(A2), .X1(A1), .X0(A0), .E__active_high(Enable),
    .R__Active_low(mystery_2_with_enable_1_r__active_low), .Z1(mystery_2_with_enable_1_z1),
    .Z0(mystery_2_with_enable_1_z0));
  mystery_2_with_enable mystery_2_with_enable_2 (
    .X3(A7), .X2(A6), .X1(A5), .X0(A4), .E__active_high(mystery_2_with_enable_1_r__active_low),
    .R__Active_low(mystery_2_with_enable_2_r__active_low), .Z1(mystery_2_with_enable_2_z1),
    .Z0(mystery_2_with_enable_2_z0));
  not not_1 (Z2, mystery_2_with_enable_2_r__active_low);
  Multiplexer #(.enable("false")) multiplexer_1 (
    .in0(mystery_2_with_enable_1_z1), .in1(mystery_2_with_enable_2_z1), .out(Z1), .sel(Z2));
  Multiplexer #(.enable("false")) multiplexer_2 (
    .in0(mystery_2_with_enable_1_z0), .in1(mystery_2_with_enable_2_z0), .out(Z0), .sel(Z2));
  and and_1 (R__Active_low, mystery_2_with_enable_2_r__active_low, mystery_2_with_enable_1_r__active_low);
endmodule

module using_library_components (
  input  _0,
  input  _1,
  input  _2,
  input  _3,
  input  _4,
  input  _5,
  input  _6,
  input  _7,
  input  _8,
  input  _9,
  input  _10,
  input  _11,
  input  _12,
  input  _13,
  input  _14,
  input  in_16,
  input  _15,
  output out_18,
  output [2:0] out_19,
  output out_20,
  output [2:0] out_21,
  output [3:0] out_22,
  output [2:0] out_23,
  output out_24
);

  wire priority_encoder_2_en_out;

  Priority_Encoder priority_encoder_1 (
    .in0(_0), .in1(_1), .in2(_2), .in3(_3), .in4(_4), .in5(_5), .in6(_6), .in7(_7), .out(out_19),
    .en_in(priority_encoder_2_en_out), .gs(out_20), .en_out(out_18));
  Priority_Encoder priority_encoder_2 (
    .in0(_8), .in1(_9), .in2(_10), .in3(_11), .in4(_12), .in5(_13), .in6(_14), .in7(_15), .out(out_23),
    .en_in(in_16), .gs(out_22[3]), .en_out(priority_encoder_2_en_out));
  Multiplexer #(.width(3)) multiplexer_1 (.in0(out_19), .in1(out_23), .out(out_21), .sel(out_22[3]), .en(1'b1));

  assign out_22[2:0] = out_21;
  assign out_24 = out_22[3];
endmodule
