// Logisim project counter.circ as structural Verilog: 3 circuits, main circuit Counter
module Counter (
  input  X_Input
);

  wire and_1_out, and_2_out, and_3_out, and_4_out, and_5_out, and_6_out, CLK, IS, not_1_out, not_2_out,
       not_3_out, not_4_out, or_1_out, or_2_out, or_3_out, Q0, Q1, Q2;

  Clock Clock (.out(CLK));
  Button Set_Initial_State (.out(IS));
  not not_1 (not_1_out, X_Input);
  and and_1 (and_1_out, not_1_out, Q2);
  and and_2 (and_2_out, X_Input, Q0);
  not not_2 (not_2_out, X_Input);
  and and_3 (and_3_out, not_2_out, Q1);
  not not_3 (not_3_out, Q2);
  and and_4 (and_4_out, not_3_out, X_Input);
  not not_4 (not_4_out, X_Input);
  and and_5 (and_5_out, not_4_out, Q0);
  and and_6 (and_6_out, X_Input, Q1);
  or or_1 (or_1_out, and_1_out, and_2_out);
  or or_2 (or_2_out, and_3_out, and_4_out);
  or or_3 (or_3_out, and_5_out, and_6_out);
  D_Flip_Flop d_ff_1 (.clk(CLK), .D(or_1_out), .Q(Q2), .preset(IS));  // open: Qn, en, reset
  D_Flip_Flop d_ff_2 (.clk(CLK), .D(or_2_out), .Q(Q1), .reset(IS));  // open: Qn, preset, en
  D_Flip_Flop d_ff_3 (.clk(CLK), .D(or_3_out), .Q(Q0), .preset(IS));  // open: Qn, en, reset

  // Other names for the same wires on the sheet: X = X_Input
endmodule

module Counter__expanded (
  input  X_Input
);

  wire and_1_out, and_2_out, and_3_out, and_4_out, and_5_out, and_6_out, CLK, IS, not_1_out, not_2_out,
       not_3_out, not_4_out, or_1_out, or_2_out, or_3_out, Q0, Q1, Q2;
  wire [3:0] bit_extender_1_out;

  Clock Clock (.out(CLK));
  Button Set_Initial_State (.out(IS));
  not not_1 (not_1_out, Q2);
  not not_2 (not_2_out, X_Input);
  not not_3 (not_3_out, Q1);
  not not_4 (not_4_out, Q0);
  and and_1 (and_1_out, not_2_out, Q2);
  and and_2 (and_2_out, X_Input, Q0);
  and and_3 (and_3_out, not_2_out, Q1);
  and and_4 (and_4_out, X_Input, not_1_out);
  and and_5 (and_5_out, not_2_out, Q0);
  and and_6 (and_6_out, X_Input, Q1);
  or or_1 (or_1_out, and_1_out, and_2_out);
  or or_2 (or_2_out, and_3_out, and_4_out);
  or or_3 (or_3_out, and_5_out, and_6_out);
  assign bit_extender_1_out = {{1{1'b0}}, {Q2, Q1, Q0}};  // Bit_Extender bit_extender_1
  D_Flip_Flop u_Q2 (.clk(CLK), .D(or_1_out), .Q(Q2), .preset(IS));  // open: Qn, en, reset
  D_Flip_Flop u_Q1 (.clk(CLK), .D(or_2_out), .Q(Q1), .reset(IS));  // open: Qn, preset, en
  D_Flip_Flop u_Q0 (.clk(CLK), .D(or_3_out), .Q(Q0), .reset(IS));  // open: Qn, preset, en
  Hex_Digit_Display hex_digit_display_1 (.value(bit_extender_1_out));  // open: dp

  // Other names for the same wires on the sheet: X = X_Input
endmodule

module Bonus (
  input  X_Input
);

  wire and_1_out, and_2_out, and_3_out, and_4_out, CLK, IS, not_1_out, not_2_out, not_3_out, not_4_out,
       or_1_out, Q0, Q1, Q2;
  wire [3:0] bit_extender_1_out;

  Clock Clock (.out(CLK));
  Button Set_Initial_State (.out(IS));
  not not_1 (not_1_out, Q2);
  not not_2 (not_2_out, X_Input);
  not not_3 (not_3_out, Q1);
  not not_4 (not_4_out, Q0);
  and and_1 (and_1_out, X_Input, Q2);
  and and_2 (and_2_out, Q1, not_4_out);
  buf and_3 (and_3_out, Q2);  // AND_Gate
  buf and_4 (and_4_out, Q1);  // AND_Gate
  or or_1 (or_1_out, and_1_out, not_3_out, and_2_out);
  assign bit_extender_1_out = {{1{1'b0}}, {Q2, Q1, Q0}};  // Bit_Extender bit_extender_1
  D_Flip_Flop u_Q2 (.clk(CLK), .D(or_1_out), .Q(Q2), .preset(IS));  // open: Qn, en, reset
  D_Flip_Flop u_Q1 (.clk(CLK), .D(and_3_out), .Q(Q1), .reset(IS));  // open: Qn, preset, en
  D_Flip_Flop u_Q0 (.clk(CLK), .D(and_4_out), .Q(Q0), .reset(IS));  // open: Qn, preset, en
  Hex_Digit_Display hex_digit_display_1 (.value(bit_extender_1_out));  // open: dp

  // Other names for the same wires on the sheet: X = X_Input
endmodule
