// Logisim project studio7.circ as structural Verilog: 2 circuits, main circuit d flip flop
module d_flip_flop (
  input  X_Input
);

  wire and_1_out, and_2_out, and_3_out, and_4_out, and_5_out, and_6_out, and_7_out, and_8_out, and_9_out,
       and_10_out, and_11_out, and_12_out, and_13_out, and_14_out, and_15_out, and_16_out, and_17_out,
       and_18_out, CLK, IS, not_1_out, not_2_out, not_3_out, not_4_out, or_1_out, or_2_out, or_3_out,
       or_4_out, or_5_out, Q0, Q1, Q2;
  wire [3:0] bit_extender_1_out;

  Clock Clock (.out(CLK));
  Button Set_Initial_State (.out(IS));
  not not_1 (not_1_out, X_Input);
  not not_2 (not_2_out, Q2);
  not not_3 (not_3_out, Q1);
  not not_4 (not_4_out, Q0);
  and and_1 (and_1_out, not_1_out, Q2);
  and and_2 (and_2_out, Q1, Q0);
  and and_3 (and_3_out, not_1_out, Q0);
  and and_4 (and_4_out, not_1_out, Q1);
  and and_5 (and_5_out, Q2, Q1);
  and and_6 (and_6_out, X_Input, not_2_out, not_3_out, not_4_out);
  and and_7 (and_7_out, Q1, not_4_out);
  and and_8 (and_8_out, Q2, Q1);
  and and_9 (and_9_out, X_Input, Q0);
  and and_10 (and_10_out, not_1_out, Q0);
  and and_11 (and_11_out, Q1, Q0);
  and and_12 (and_12_out, not_2_out, Q0);
  and and_13 (and_13_out, Q2, not_3_out, not_4_out);
  and and_14 (and_14_out, X_Input, not_2_out, Q1);
  and and_15 (and_15_out, Q2, Q1, not_4_out);
  and and_16 (and_16_out, not_2_out, not_3_out, not_4_out);
  and and_17 (and_17_out, Q2, Q1, Q0);
  and and_18 (and_18_out, not_2_out, not_3_out, not_4_out);
  or or_1 (or_1_out, and_15_out, and_16_out);
  or or_2 (or_2_out, and_17_out, and_18_out);
  assign bit_extender_1_out = {{1{1'b0}}, {Q2, Q1, Q0}};  // Bit_Extender bit_extender_1
  or or_3 (or_3_out, and_1_out, and_2_out, and_3_out, and_4_out, and_5_out, and_6_out);
  or or_4 (or_4_out, and_7_out, and_8_out, and_9_out);
  or or_5 (or_5_out, and_10_out, and_11_out, and_12_out, and_13_out, and_14_out);
  LED Z1 (.in(or_1_out));
  LED Z0 (.in(or_2_out));
  Hex_Digit_Display hex_digit_display_1 (.value(bit_extender_1_out));  // open: dp
  D_Flip_Flop u_Q2 (.clk(CLK), .D(or_3_out), .Q(Q2), .reset(IS));  // open: Qn, preset, en
  D_Flip_Flop u_Q1 (.clk(CLK), .D(or_4_out), .Q(Q1), .reset(IS));  // open: Qn, preset, en
  D_Flip_Flop u_Q0 (.clk(CLK), .D(or_5_out), .Q(Q0), .reset(IS));  // open: Qn, preset, en

  // Other names for the same wires on the sheet: X = X_Input
endmodule

module t_flip_flop (
  input  X_Input
);

  wire and_1_out, and_2_out, and_3_out, and_4_out, and_5_out, and_6_out, and_7_out, and_8_out, and_9_out,
       and_10_out, and_11_out, and_12_out, and_13_out, and_14_out, CLK, IS, not_1_out, not_2_out, not_3_out,
       not_4_out, or_1_out, or_2_out, or_3_out, or_4_out, or_5_out, Q0, Q1, Q2;
  wire [3:0] bit_extender_1_out;

  Clock Clock (.out(CLK));
  Button Set_Initial_State (.out(IS));
  not not_1 (not_1_out, X_Input);
  not not_2 (not_2_out, Q2);
  not not_3 (not_3_out, Q0);
  not not_4 (not_4_out, Q1);
  and and_1 (and_1_out, X_Input, not_4_out, not_3_out);
  and and_2 (and_2_out, not_2_out, Q1, Q0);
  and and_3 (and_3_out, X_Input, Q2, not_4_out);
  and and_4 (and_4_out, not_1_out, not_2_out, Q0);
  and and_5 (and_5_out, not_1_out, not_2_out, Q1);
  and and_6 (and_6_out, X_Input, not_4_out, Q0);
  and and_7 (and_7_out, not_1_out, not_2_out, Q1, Q0);
  and and_8 (and_8_out, not_3_out, not_4_out, Q2);
  and and_9 (and_9_out, X_Input, Q2, not_4_out);
  and and_10 (and_10_out, X_Input, not_2_out, Q1, not_3_out);
  and and_11 (and_11_out, Q2, Q1, not_3_out);
  and and_12 (and_12_out, not_2_out, not_4_out, not_3_out);
  and and_13 (and_13_out, Q2, Q1, Q0);
  and and_14 (and_14_out, not_2_out, not_4_out, not_3_out);
  or or_1 (or_1_out, and_1_out, and_2_out, and_3_out, and_4_out, and_5_out);
  or or_2 (or_2_out, and_6_out, and_7_out);
  or or_3 (or_3_out, and_8_out, and_9_out, and_10_out);
  or or_4 (or_4_out, and_11_out, and_12_out);
  or or_5 (or_5_out, and_13_out, and_14_out);
  assign bit_extender_1_out = {{1{1'b0}}, {Q2, Q1, Q0}};  // Bit_Extender bit_extender_1
  T_Flip_Flop t_ff_1 (.clk(CLK), .T(or_1_out), .Q(Q2), .reset(IS));  // open: Qn, preset, en
  T_Flip_Flop t_ff_2 (.clk(CLK), .T(or_2_out), .Q(Q1), .reset(IS));  // open: Qn, preset, en
  T_Flip_Flop t_ff_3 (.clk(CLK), .T(or_3_out), .Q(Q0), .reset(IS));  // open: Qn, preset, en
  LED Z1 (.in(or_4_out));
  LED Z0 (.in(or_5_out));
  Hex_Digit_Display hex_digit_display_1 (.value(bit_extender_1_out));  // open: dp

  // Other names for the same wires on the sheet: X = X_Input
endmodule
