// Logisim project studio8_tff.circ as structural Verilog: 4 circuits, main circuit Input Encoder
// Input
module Input_Encoder (
  input  N,
  input  D,
  input  Q,
  output out_4,
  output out_5
);

  Priority_Encoder #(.select(2), .disabled(0)) priority_encoder_1 (
    .in0(1'b1), .in1(N), .in2(D), .in3(Q), .out({out_5, out_4}));  // open: gs, en_out, en_in
endmodule

module State_Machine (
  input  X1,
  input  in_2,
  input  X0,
  output out_4,
  output out_5,
  output Y1,
  output Y0
);

  wire and_1_out, and_2_out, and_3_out, and_4_out, and_5_out, and_6_out, not_1_out, not_2_out, not_3_out,
       or_1_out, or_2_out;

  not not_1 (not_1_out, X0);
  not not_2 (not_2_out, X1);
  not not_3 (not_3_out, X1);
  and and_1 (and_1_out, X1, not_1_out);
  and and_2 (and_2_out, X1, Y1);
  and and_3 (and_3_out, not_2_out, X0, Y0);
  and and_4 (and_4_out, not_3_out, X0);
  and and_5 (and_5_out, X0, Y0);
  and and_6 (and_6_out, X1, Y1, Y0);
  or or_1 (or_1_out, and_1_out, and_2_out, and_3_out);
  or or_2 (or_2_out, and_4_out, and_5_out, and_6_out);
  T_Flip_Flop t_ff_1 (.clk(in_2), .T(or_1_out), .Q(Y1));  // open: Qn, preset, reset, en
  T_Flip_Flop t_ff_2 (.clk(in_2), .T(or_2_out), .Q(Y0));  // open: Qn, preset, reset, en

  assign out_4 = X1;
  assign out_5 = X0;

  // Other names for the same wires on the sheet: CLK = in_2
endmodule

module Output_Decoder (
  input  X1,
  input  X0,
  input  Y1,
  input  Y0,
  output R,
  output _0,
  output _5,
  output _10,
  output _15,
  output _20
);

  wire and_1_out, and_2_out, and_3_out, and_4_out, and_5_out, and_6_out, and_7_out, and_8_out, and_9_out,
       and_10_out, and_11_out, and_12_out, not_1_out, not_2_out, not_3_out, not_4_out, not_5_out, not_6_out,
       not_7_out, not_8_out, not_9_out, not_10_out, not_11_out, not_12_out, not_13_out, not_14_out,
       not_15_out, not_16_out, not_17_out, not_18_out, not_19_out, not_20_out, not_21_out, Z0, Z1, Z2;

  not not_1 (not_1_out, X0);
  not not_2 (not_2_out, Y0);
  not not_3 (not_3_out, Y0);
  not not_4 (not_4_out, Y0);
  not not_5 (not_5_out, X1);
  not not_6 (not_6_out, Y0);
  not not_7 (not_7_out, X0);
  not not_8 (not_8_out, X1);
  and and_1 (and_1_out, X0, Y1, Y0);
  and and_2 (and_2_out, X1, not_1_out, Y1, not_2_out);
  and and_3 (and_3_out, X1, Y1, not_3_out);
  and and_4 (and_4_out, X1, X0, Y1, not_4_out);
  and and_5 (and_5_out, not_5_out, X0, Y1, Y0);
  and and_6 (and_6_out, X1, X0, not_6_out);
  and and_7 (and_7_out, X1, not_7_out, Y1);
  and and_8 (and_8_out, not_8_out, X0, Y1, Y0);
  or or_1 (Z2, and_1_out, and_2_out);
  or or_2 (Z1, and_3_out, and_4_out, and_5_out);
  or or_3 (Z0, and_6_out, and_7_out, and_8_out);
  not not_9 (not_9_out, X1);
  not not_10 (not_10_out, Y1);
  not not_11 (not_11_out, X1);
  not not_12 (not_12_out, X1);
  not not_13 (not_13_out, X0);
  not not_14 (not_14_out, X0);
  and and_9 (and_9_out, not_14_out, not_15_out);
  not not_15 (not_15_out, Y1);
  and and_10 (and_10_out, not_9_out, not_10_out);
  and and_11 (and_11_out, not_11_out, Y0);
  and and_12 (and_12_out, not_12_out, not_13_out);
  not not_16 (not_16_out, Z2);
  not not_17 (not_17_out, Z1);
  not not_18 (not_18_out, Z2);
  not not_19 (not_19_out, Z1);
  not not_20 (not_20_out, Z0);
  and and_13 (R, and_10_out, and_11_out, and_12_out, and_9_out);
  and and_14 (_0, Z2, Z1, Z0);
  and and_15 (_5, not_16_out, not_17_out, Z0);
  and and_16 (_15, not_18_out, Z1, Z0);
  and and_17 (_20, Z2, not_19_out, not_20_out);
  not not_21 (not_21_out, Y1);
  and and_18 (_10, X1, X0, not_21_out, Y0);
endmodule

module Controller (
  input  Nickel,
  input  Dime,
  input  Quarter,
  output No_candy,
  output No_change,
  output _5c_change,
  output _10c_change,
  output _15c_change,
  output _20c_change
);

  wire CLK, input_encoder_1_out_4, input_encoder_1_out_5, state_machine_1_out_4, state_machine_1_out_5,
       state_machine_1_y0, state_machine_1_y1;

  Clock clock_1 (.out(CLK));
  Input_Encoder input_encoder_1 (
    .N(Nickel), .D(Dime), .Q(Quarter), .out_4(input_encoder_1_out_4), .out_5(input_encoder_1_out_5));
  State_Machine state_machine_1 (
    .out_4(state_machine_1_out_4), .X1(input_encoder_1_out_5), .in_2(CLK), .X0(input_encoder_1_out_4),
    .out_5(state_machine_1_out_5), .Y1(state_machine_1_y1), .Y0(state_machine_1_y0));
  Output_Decoder output_decoder_1 (
    .X1(state_machine_1_out_4), .X0(state_machine_1_out_5), .Y1(state_machine_1_y1), .Y0(state_machine_1_y0),
    .R(No_candy), ._0(No_change), ._5(_5c_change), ._15(_15c_change), ._20(_20c_change), ._10(_10c_change));

  // Other names for the same wires on the sheet: D = Dime; N = Nickel; Q = Quarter
endmodule
