// Logisim project studio9.circ as structural Verilog: 3 circuits, main circuit 2 Level
module _2_Level (
  input  Cin,
  input  X1,
  input  X0,
  input  Y1,
  input  Y0,
  output Cout,
  output D1,
  output D0
);

  wire and_1_out, and_2_out, and_3_out, and_4_out, and_5_out, and_6_out, and_7_out, and_8_out, and_9_out,
       and_10_out, and_11_out, and_12_out, and_13_out, and_14_out, and_15_out, and_16_out, and_17_out,
       and_18_out, and_19_out, and_20_out, and_21_out, and_22_out, and_23_out, not_1_out, not_2_out,
       not_3_out, not_4_out, not_5_out;

  not not_1 (not_1_out, Cin);
  not not_2 (not_2_out, X1);
  not not_3 (not_3_out, X0);
  not not_4 (not_4_out, Y1);
  not not_5 (not_5_out, Y0);
  and and_1 (and_1_out, Cin, X1, X0);
  and and_2 (and_2_out, Cin, X1, Y0);
  and and_3 (and_3_out, Cin, Y1, Y0);
  and and_4 (and_4_out, Cin, X0, Y1);
  and and_5 (and_5_out, X1, Y1);
  and and_6 (and_6_out, X1, X0, Y0);
  and and_7 (and_7_out, X0, Y1, Y0);
  and and_8 (and_8_out, Cin, not_2_out, X0, not_4_out);
  and and_9 (and_9_out, Cin, not_2_out, not_4_out, Y0);
  and and_10 (and_10_out, Cin, X1, Y1, Y0);
  and and_11 (and_11_out, Cin, X1, X0, Y1);
  and and_12 (and_12_out, X1, X0, Y1, Y0);
  and and_13 (and_13_out, not_2_out, not_3_out, Y1, not_5_out);
  and and_14 (and_14_out, not_2_out, X0, not_4_out, Y0);
  and and_15 (and_15_out, X1, not_3_out, not_4_out, not_5_out);
  and and_16 (and_16_out, not_1_out, X1, not_4_out, not_5_out);
  and and_17 (and_17_out, not_1_out, X1, not_3_out, not_4_out);
  and and_18 (and_18_out, not_1_out, not_2_out, not_3_out, Y1);
  and and_19 (and_19_out, not_1_out, not_2_out, Y1, not_5_out);
  and and_20 (and_20_out, Cin, X0, Y0);
  and and_21 (and_21_out, Cin, not_3_out, not_5_out);
  and and_22 (and_22_out, not_1_out, not_3_out, Y0);
  and and_23 (and_23_out, not_1_out, X0, not_5_out);
  or or_1 (D0, and_20_out, and_21_out, and_22_out, and_23_out);
  or or_2 (Cout, and_1_out, and_2_out, and_3_out, and_4_out, and_5_out, and_6_out, and_7_out);
  or or_3 (D1, and_8_out, and_9_out, and_10_out, and_11_out, and_12_out, and_13_out, and_14_out, and_15_out, and_16_out, and_17_out, and_18_out, and_19_out);
endmodule

module n_bit_adder (
  input  A15,
  input  A14,
  input  A13,
  input  A12,
  input  A11,
  input  A10,
  input  A9,
  input  A8,
  input  A7,
  input  A6,
  input  A5,
  input  A4,
  input  A3,
  input  A2,
  input  A1,
  input  A0,
  input  B15,
  input  B14,
  input  B13,
  input  B12,
  input  B11,
  input  B10,
  input  B9,
  input  B8,
  input  B7,
  input  B6,
  input  B5,
  input  B4,
  input  B3,
  input  B2,
  input  B1,
  input  B0,
  input  Cin,
  output S15,
  output S14,
  output S13,
  output S12,
  output S11,
  output S10,
  output S9,
  output S8,
  output S7,
  output S6,
  output S5,
  output S4,
  output S3,
  output S2,
  output S1,
  output S0,
  output Overflow
);

  wire n2_level_2_cout, n2_level_3_cout, n2_level_4_cout, n2_level_5_cout, n2_level_6_cout, n2_level_7_cout,
       n2_level_8_cout, xnor_1_out, xor_1_out;

  xnor xnor_1 (xnor_1_out, A15, B15);
  xor xor_1 (xor_1_out, B15, S15);
  and and_1 (Overflow, xnor_1_out, xor_1_out);
  _2_Level u_2_level_1 (
    .D1(S15), .D0(S14), .Cin(n2_level_2_cout), .X1(A15), .X0(A14), .Y1(B15), .Y0(B14));  // open: Cout
  _2_Level u_2_level_2 (
    .Cout(n2_level_2_cout), .D1(S13), .D0(S12), .Cin(n2_level_3_cout), .X1(A13), .X0(A12), .Y1(B13), .Y0(B12));
  _2_Level u_2_level_3 (
    .Cout(n2_level_3_cout), .D1(S11), .D0(S10), .Cin(n2_level_4_cout), .X1(A11), .X0(A10), .Y1(B11), .Y0(B10));
  _2_Level u_2_level_4 (
    .Cout(n2_level_4_cout), .D1(S9), .D0(S8), .Cin(n2_level_5_cout), .X1(A9), .X0(A8), .Y1(B9), .Y0(B8));
  _2_Level u_2_level_5 (
    .Cout(n2_level_5_cout), .D1(S7), .D0(S6), .Cin(n2_level_6_cout), .X1(A7), .X0(A6), .Y1(B7), .Y0(B6));
  _2_Level u_2_level_6 (
    .Cout(n2_level_6_cout), .D1(S5), .D0(S4), .Cin(n2_level_7_cout), .X1(A5), .X0(A4), .Y1(B5), .Y0(B4));
  _2_Level u_2_level_7 (
    .Cout(n2_level_7_cout), .D1(S3), .D0(S2), .Cin(n2_level_8_cout), .X1(A3), .X0(A2), .Y1(B3), .Y0(B2));
  _2_Level u_2_level_8 (.Cout(n2_level_8_cout), .D1(S1), .D0(S0), .Cin(Cin), .X1(A1), .X0(A0), .Y1(B1), .Y0(B0));
endmodule

module Add_Subtract (
  input  B15,
  input  B14,
  input  B13,
  input  B12,
  input  B11,
  input  B10,
  input  B9,
  input  B8,
  input  B7,
  input  B6,
  input  B5,
  input  B4,
  input  B3,
  input  B2,
  input  B1,
  input  B0,
  input  Subtract_Add,
  input  A15,
  input  A14,
  input  A13,
  input  A12,
  input  A11,
  input  A10,
  input  A9,
  input  A8,
  input  A7,
  input  A6,
  input  A5,
  input  A4,
  input  A3,
  input  A2,
  input  A1,
  input  A0,
  output Overflow,
  output S15,
  output S14,
  output S13,
  output S12,
  output S11,
  output S10,
  output S9,
  output S8,
  output S7,
  output S6,
  output S5,
  output S4,
  output S3,
  output S2,
  output S1,
  output S0
);

  wire not_1_out, xor_1_out, xor_2_out, xor_3_out, xor_4_out, xor_5_out, xor_6_out, xor_7_out, xor_8_out,
       xor_9_out, xor_10_out, xor_11_out, xor_12_out, xor_13_out, xor_14_out, xor_15_out, xor_16_out;

  xor xor_1 (xor_1_out, not_1_out, B13);
  xor xor_2 (xor_2_out, not_1_out, B15);
  xor xor_3 (xor_3_out, not_1_out, B14);
  xor xor_4 (xor_4_out, not_1_out, B12);
  xor xor_5 (xor_5_out, not_1_out, B11);
  xor xor_6 (xor_6_out, not_1_out, B10);
  xor xor_7 (xor_7_out, not_1_out, B9);
  xor xor_8 (xor_8_out, not_1_out, B7);
  xor xor_9 (xor_9_out, not_1_out, B8);
  xor xor_10 (xor_10_out, not_1_out, B6);
  xor xor_11 (xor_11_out, not_1_out, B5);
  xor xor_12 (xor_12_out, not_1_out, B4);
  xor xor_13 (xor_13_out, not_1_out, B2);
  xor xor_14 (xor_14_out, not_1_out, B3);
  n_bit_adder n_bit_adder_1 (
    .Cin(not_1_out), .A15(A15), .B15(xor_2_out), .A14(A14), .B14(xor_3_out), .A13(A13), .B13(xor_1_out),
    .A12(A12), .B12(xor_4_out), .A11(A11), .B11(xor_5_out), .A10(A10), .B10(xor_6_out), .A9(A9),
    .B9(xor_7_out), .A8(A8), .B8(xor_9_out), .A7(A7), .B7(xor_8_out), .A6(A6), .B6(xor_10_out), .A5(A5),
    .B5(xor_11_out), .A4(A4), .B4(xor_12_out), .A3(A3), .B3(xor_14_out), .A2(A2), .B2(xor_13_out), .A1(A1),
    .B1(xor_15_out), .A0(A0), .B0(xor_16_out), .Overflow(Overflow), .S15(S15), .S14(S14), .S13(S13),
    .S12(S12), .S11(S11), .S10(S10), .S9(S9), .S8(S8), .S7(S7), .S6(S6), .S5(S5), .S4(S4), .S3(S3), .S2(S2),
    .S1(S1), .S0(S0));
  xor xor_15 (xor_15_out, not_1_out, B1);
  xor xor_16 (xor_16_out, not_1_out, B0);
  not not_1 (not_1_out, Subtract_Add);
endmodule
